# Fritzing sketch DemoBoard (saved by Fritzing 0.9.2b)
breadboards: 1

parts:
  R1 = Resistor [tolerance=±5% resistance=22k package=THT]
  R2 = Photocell (LDR) [part_number=VT90N2 package=THT]
  J1 = male pin header, 3 pins [form="♂ (male)"]
  U1 = atmega328 [package=dip]
  J2 = double row male pin header, 6 pins [form="♂ (male)"]
  R3 = Resistor [tolerance=±5% resistance=10k package=THT]
  C1 = Ceramic Capacitor [capacitance=1µF package="100 mil [THT, multilayer]"]
  XTAL1 = Crystal [frequency="16 Mhz" package=THT]
  Red_Button = Pushbutton [package=THT]
  Yellow_Button = Pushbutton [package=THT]
  C2 = Ceramic Capacitor [capacitance=22pF package="100 mil [THT, multilayer]"]
  C3 = Ceramic Capacitor [capacitance=22pF package="100 mil [THT, multilayer]"]
  R4 = Resistor [tolerance=±20% resistance=10k package=THT]
  R5 = Resistor [tolerance=±5% resistance=10k package=THT]
  R6 = Resistor [tolerance=±5% resistance=220 package=THT]
  Yellow_LED = LED - 5mm [color="Yellow (595nm)" package="5 mm [THT]"]
  R7 = Resistor [tolerance=±5% resistance=220 package=THT]
  R8 = Resistor [tolerance=±5% resistance=220 package=THT]
  Red_LED = LED - 5mm [color="Red (633nm)" package="5 mm [THT]"]
  Green_LED = LED - 5mm [color="Green (555nm)" package="5 mm [THT]"]

nets:
  N1: R1.Pin_0, R2.pin_0, U1.A4
  N2: R1.Pin_1, J1.pin1, U1.GND, C2.0, C3.0, R4.Pin_0, R5.Pin_0, Yellow_LED.cathode, Red_LED.cathode, Green_LED.cathode
  N3: R2.pin_1, J1.pin2, U1.VCC, U1.AVCC, U1.AREF, J2.pin4, J2.pin6, R3.Pin_0, Red_Button.leg0, Yellow_Button.leg0, R6.Pin_0
  N4: J1.pin3, U1.D10_(PWM)
  N5: U1.RESET, R3.Pin_1, C1.0
  N6: U1.D0_(RX), J2.pin3
  N7: U1.D1_(TX), J2.pin2
  N8: U1.XLAT1, XTAL1.pin_1, C2.1
  N9: U1.XLAT2, XTAL1.pin_0, C3.1
  N10: U1.D6_(PWM), Red_Button.leg1, R4.Pin_1
  N11: U1.D7, Yellow_Button.leg1, R5.Pin_1
  N12: U1.D8, R8.Pin_0
  N13: U1.D9_(PWM), R7.Pin_0
  N14: J2.pin1, C1.1
  N15: R6.Pin_1, Yellow_LED.anode
  N16: R7.Pin_1, Red_LED.anode
  N17: R8.Pin_1, Green_LED.anode
